# Fritzing sketch project sketch (saved by Fritzing 0.9.2b)
breadboards: 1

parts:
  Part1 = Intel Galileo
  R1 = Resistor [tolerance=±5% resistance=100 package=THT]
  R2 = Resistor [tolerance=±5% resistance=10k package=THT]
  Q1 = NPN-Transistor [package="TO92 [THT]"]

nets:
  N1: Part1.D2, R2.Pin_0, Q1.E
  N2: Part1.3V3, R1.Pin_1, Q1.C
  N3: Part1.GND, R2.Pin_1
